// Logisim project DSD_Lab5_1.circ as structural Verilog: 3 circuits, main circuit main
module main (
  input  B,
  input  C,
  input  A,
  input  I1,
  input  I2,
  input  I3,
  input  I4,
  input  I5,
  input  I6,
  input  I7,
  input  I8,
  output out_12
);

  wire and_1_out, and_2_out, and_3_out, and_4_out, and_5_out, and_6_out, and_7_out, and_8_out, and_9_out,
       and_10_out, and_11_out, and_12_out, and_13_out, and_14_out, and_15_out, and_16_out, not_1_out,
       not_2_out, not_3_out;

  not not_1 (not_1_out, A);
  not not_2 (not_2_out, B);
  not not_3 (not_3_out, C);
  and and_1 (and_1_out, not_1_out, not_2_out, not_3_out);
  and and_2 (and_2_out, not_1_out, not_2_out, C);
  and and_3 (and_3_out, not_1_out, B, not_3_out);
  and and_4 (and_4_out, not_1_out, B, C);
  and and_5 (and_5_out, A, not_2_out, not_3_out);
  and and_6 (and_6_out, A, not_2_out, C);
  and and_7 (and_7_out, A, B, not_3_out);
  and and_8 (and_8_out, A, B, C);
  and and_9 (and_9_out, and_1_out, I1);
  and and_10 (and_10_out, and_2_out, I2);
  and and_11 (and_11_out, and_3_out, I3);
  and and_12 (and_12_out, and_4_out, I4);
  and and_13 (and_13_out, and_5_out, I5);
  and and_14 (and_14_out, and_6_out, I6);
  and and_15 (and_15_out, and_7_out, I7);
  and and_16 (and_16_out, and_8_out, I8);
  or or_1 (out_12, and_9_out, and_10_out, and_11_out, and_12_out, and_13_out, and_14_out, and_15_out, and_16_out);
endmodule

module decode (
  input  in_1,
  input  in_2,
  input  in_3,
  output out_4,
  output out_5,
  output out_6,
  output out_7,
  output out_8,
  output out_9,
  output out_10,
  output out_11
);

  wire not_1_out, not_2_out, not_3_out;

  not not_1 (not_1_out, in_3);
  not not_2 (not_2_out, in_1);
  not not_3 (not_3_out, in_2);
  and and_1 (out_4, not_1_out, not_2_out, not_3_out);
  and and_2 (out_5, not_1_out, not_2_out, in_2);
  and and_3 (out_6, not_1_out, in_1, not_3_out);
  and and_4 (out_7, not_1_out, in_1, in_2);
  and and_5 (out_8, in_3, not_2_out, not_3_out);
  and and_6 (out_9, in_3, not_2_out, in_2);
  and and_7 (out_10, in_3, in_1, not_3_out);
  and and_8 (out_11, in_3, in_1, in_2);
endmodule

module test (
  input  in_1,
  input  in_2,
  input  in_3,
  input  in_4,
  input  in_5,
  input  in_6,
  input  in_7,
  input  in_8,
  input  in_9,
  input  in_10,
  input  in_11,
  output out_12
);

  wire and_1_out, and_2_out, and_3_out, and_4_out, and_5_out, and_6_out, and_7_out, and_8_out,
       decode_1_out_4, decode_1_out_5, decode_1_out_6, decode_1_out_7, decode_1_out_8, decode_1_out_9,
       decode_1_out_10, decode_1_out_11;

  decode decode_1 (
    .in_1(in_5), .in_2(in_6), .in_3(in_7), .out_4(decode_1_out_4), .out_5(decode_1_out_5),
    .out_6(decode_1_out_6), .out_7(decode_1_out_7), .out_8(decode_1_out_8), .out_9(decode_1_out_9),
    .out_10(decode_1_out_10), .out_11(decode_1_out_11));
  and and_1 (and_1_out, in_1, decode_1_out_4);
  and and_2 (and_2_out, in_2, decode_1_out_5);
  and and_3 (and_3_out, in_3, decode_1_out_6);
  and and_4 (and_4_out, in_4, decode_1_out_7);
  and and_5 (and_5_out, in_8, decode_1_out_8);
  and and_6 (and_6_out, in_9, decode_1_out_9);
  and and_7 (and_7_out, in_10, decode_1_out_11);
  and and_8 (and_8_out, in_11, decode_1_out_10);
  or or_1 (out_12, and_1_out, and_2_out, and_3_out, and_4_out, and_5_out, and_6_out, and_7_out, and_8_out);
endmodule
